# Fritzing sketch RP2040-Zero-ModXo (saved by Fritzing 0.9.5d)
circuit board: 3.85676cm x 2.83541cm
perfboards: 1

parts:
  RP2040-ZERO = Waveshare rp2040-zero tht [package=THT]
  R4 = Resistor [tolerance=±5% resistance=100 package=THT]
  R3 = Resistor [tolerance=±5% resistance=100 package=THT]
  R2 = Resistor [tolerance=±5% resistance=100 package=THT]
  R1 = Resistor [tolerance=±5% resistance=100 package=THT]
  J5 = female pin header, 3 pins [form="♀ (female)"]
  J2 = female pin header, 3 pins [form="♀ (female)"]
  LCLK = female pin header, 2 pins [form="♀ (female)"]
  GND = female pin header, 1 pin [form="♀ (female)"]
  D0 = male pin header, 1 pin [form="♂ (male)"]
  J3 = female pin header, 1 pin [form="♀ (female)"]  # not connected
  J4 = female pin header, 1 pin [form="♀ (female)"]  # not connected

nets:
  5V: RP2040-ZERO.Pin_1, J2.pin3
  GND: RP2040-ZERO.Pin_2, GND.pin1
  N1: RP2040-ZERO.Pin_17, D0.pin1
  N2: RP2040-ZERO.Pin_18, LCLK.pin1
  N3: RP2040-ZERO.Pin_19, LCLK.pin2
  N4: RP2040-ZERO.Pin_20, R4.Pin_0
  N5: RP2040-ZERO.Pin_21, R3.Pin_0
  N6: RP2040-ZERO.Pin_22, R2.Pin_0
  N7: RP2040-ZERO.Pin_23, R1.Pin_0
  N8: R4.Pin_1, J5.pin3
  N9: R3.Pin_1, J2.pin2
  N10: R2.Pin_1, J2.pin1
  N11: R1.Pin_1, J5.pin1

notes:
  To back of XBOX
  TOP
  ModXo compatible
  www.consolemods.org/wiki/Xbox:Original_Xbox_Mods_Wiki#modxo
  to front
  github.com/shalxmva/modxo
  modchip

custom parts:
  Waveshare rp2040-zero tht: .RP2040-Zero, A Low-Cost, High-Performance Pico-Like MCU Board Based On Raspberry Pi Microcontroller RP2040. This varant is THT without the extra connections.
